# Fritzing sketch ultimate_machine (saved by Fritzing 0.7.10b)
breadboards: 1

parts:
  Arduino1 = Arduino
  S2 = Pushbutton [package=THT]
  J1 = Basic Servo
  R1 = 10k Ω Resistor [package=THT]

nets:
  N1: Arduino1.D9, J1.pulse
  N2: Arduino1.D2, S2.leg1, R1.Pin_0
  +5V: Arduino1.+5V, J1.vcc, R1.Pin_1
  GND: Arduino1.GND, S2.leg0, J1.gnd

notes:
  10k resistor
